# Fritzing sketch hardware (saved by Fritzing 0.9.3b)

parts:
  Raspberry_Pi_1 = Raspberry Pi 3 [part_number=RPI-3-V1.2]
  CAMERA2 = TTL Serial JPEG Camera  # not connected
  S1 = SWITCH-MOMENTARY-2 [package=tactile-pth-12mm]
  LED1 = smd LED [color="Red (633nm)" package="1206 [SMD]"]

nets:
  N1: Raspberry_Pi_1.GND, LED1.cathode
  N2: Raspberry_Pi_1.GPIO17, S1.1
  N3: Raspberry_Pi_1.GPIO18, LED1.anode

custom parts:
  TTL Serial JPEG Camera: TTL Serial JPEG Camera with NTSC Out
